# Fritzing sketch gpioLab (saved by Fritzing 0.7.5b)
breadboards: 1

parts:
  BeagleBone1 = beaglebone-a5
  R1 = Resistor [tolerance=±5% resistance=220 package=THT]
  LED1 = LED - 5mm [color="Red (633nm)" package="5 mm [THT]"]

nets:
  N1: BeagleBone1.connectorp9-3, R1.Pin_1
  N2: BeagleBone1.connectorp9-11, LED1.cathode
  N3: R1.Pin_0, LED1.anode
